// Logisim project Projeto02_CD.circ as structural Verilog
module main (
  input  Bit1,
  input  Bit2,
  input  Bit3,
  input  Bit4
);
endmodule

module SomadorCompleto (
  input  Carry_In,
  input  A,
  input  B,
  output Soma,
  output Carry_Out
);

  wire and_1_out, and_2_out, xor_1_out;

  and and_1 (and_1_out, A, B);
  xor xor_1 (xor_1_out, A, B);
  and and_2 (and_2_out, xor_1_out, Carry_In);
  or or_1 (Carry_Out, and_1_out, and_2_out);
  xor xor_2 (Soma, Carry_In, xor_1_out);
endmodule

module UnidadeSoma (
  input  Bit1A,
  input  Bit1B,
  input  Bit2A,
  input  Bit2B,
  input  Bit3A,
  input  Bit3B,
  input  Bit4A,
  input  Bit4B,
  input  Operacao,
  output Carry_Out,
  output Soma1,
  output Soma2,
  output Soma3,
  output Soma4
);

  wire somadorcompleto_2_carry_out, somadorcompleto_3_carry_out, somadorcompleto_4_carry_out, xor_1_out,
       xor_2_out, xor_3_out, xor_4_out;

  xor xor_1 (xor_1_out, Operacao, Bit1B);
  SomadorCompleto somadorcompleto_1 (
    .A(xor_1_out), .B(Bit1A), .Carry_In(somadorcompleto_2_carry_out), .Carry_Out(Carry_Out), .Soma(Soma1));
  xor xor_2 (xor_2_out, Operacao, Bit2B);
  SomadorCompleto somadorcompleto_2 (
    .A(xor_2_out), .B(Bit2A), .Carry_In(somadorcompleto_3_carry_out),
    .Carry_Out(somadorcompleto_2_carry_out), .Soma(Soma2));
  xor xor_3 (xor_3_out, Operacao, Bit3B);
  SomadorCompleto somadorcompleto_3 (
    .A(xor_3_out), .B(Bit3A), .Carry_In(somadorcompleto_4_carry_out),
    .Carry_Out(somadorcompleto_3_carry_out), .Soma(Soma3));
  xor xor_4 (xor_4_out, Operacao, Bit4B);
  SomadorCompleto somadorcompleto_4 (
    .A(xor_4_out), .B(Bit4A), .Carry_In(Operacao), .Carry_Out(somadorcompleto_4_carry_out), .Soma(Soma4));
endmodule

module DecodificadorOperando (
  input  Bit1,
  input  Bit2,
  input  Bit3,
  input  Bit4,
  output a,
  output f,
  output b,
  output g,
  output e,
  output c,
  output d,
  output DP
);

  wire and_1_out, and_2_out, and_3_out, and_4_out, and_5_out, and_6_out, and_7_out, and_8_out, and_9_out,
       and_10_out, and_11_out, and_12_out, and_13_out, and_14_out, and_15_out, and_16_out, and_17_out,
       and_18_out, and_19_out, and_20_out, not_1_out, not_2_out, not_3_out, not_4_out, not_5_out, not_6_out,
       not_7_out, not_8_out, not_9_out, not_10_out, not_11_out, not_12_out, not_13_out, not_14_out,
       not_15_out, not_16_out, not_17_out, not_18_out, not_19_out, not_20_out, not_21_out, not_22_out,
       not_23_out, not_24_out, not_25_out, not_26_out, not_27_out, not_28_out, not_29_out, not_30_out;

  not not_1 (not_1_out, Bit1);
  not not_2 (not_2_out, Bit2);
  not not_3 (not_3_out, Bit3);
  not not_4 (not_4_out, Bit3);
  not not_5 (not_5_out, Bit4);
  not not_6 (not_6_out, Bit1);
  not not_7 (not_7_out, Bit3);
  not not_8 (not_8_out, Bit1);
  not not_9 (not_9_out, Bit4);
  not not_10 (not_10_out, Bit2);
  not not_11 (not_11_out, Bit1);
  not not_12 (not_12_out, Bit2);
  not not_13 (not_13_out, Bit4);
  not not_14 (not_14_out, Bit4);
  not not_15 (not_15_out, Bit2);
  and and_1 (and_1_out, not_15_out, not_16_out, Bit4);
  not not_16 (not_16_out, Bit3);
  and and_2 (and_2_out, Bit2, not_17_out, not_18_out);
  not not_17 (not_17_out, Bit3);
  not not_18 (not_18_out, Bit4);
  and and_3 (and_3_out, Bit2, Bit3, Bit4);
  and and_4 (and_4_out, Bit2, not_19_out);
  not not_19 (not_19_out, Bit3);
  not not_20 (not_20_out, Bit2);
  not not_21 (not_21_out, Bit3);
  and and_5 (and_5_out, not_20_out, not_21_out, Bit4);
  not not_22 (not_22_out, Bit1);
  not not_23 (not_23_out, Bit2);
  and and_6 (and_6_out, not_22_out, not_23_out, Bit3);
  not not_24 (not_24_out, Bit1);
  and and_7 (and_7_out, not_24_out, Bit3, Bit4);
  not not_25 (not_25_out, Bit3);
  and and_8 (and_8_out, Bit1, not_25_out, Bit4);
  and and_9 (and_9_out, Bit1, Bit2, Bit3);
  not not_26 (not_26_out, Bit1);
  and and_10 (and_10_out, not_26_out, not_27_out, not_28_out);
  not not_27 (not_27_out, Bit2);
  not not_28 (not_28_out, Bit3);
  not not_29 (not_29_out, Bit2);
  not not_30 (not_30_out, Bit3);
  and and_11 (and_11_out, not_29_out, not_30_out, Bit4);
  and and_12 (and_12_out, Bit2, Bit3, Bit4);
  not not_31 (DP, Bit1);
  and and_13 (and_13_out, not_1_out, not_2_out, not_3_out, Bit4);
  and and_14 (and_14_out, Bit2, not_4_out, not_5_out);
  or or_1 (a, and_13_out, and_14_out, and_15_out);
  and and_15 (and_15_out, Bit1, Bit2, Bit3, Bit4);
  and and_16 (and_16_out, not_6_out, Bit2, not_7_out, Bit4);
  or or_2 (b, and_16_out, and_17_out, and_18_out);
  and and_17 (and_17_out, not_8_out, Bit2, Bit3, not_9_out);
  and and_18 (and_18_out, Bit1, not_10_out, Bit3);
  and and_19 (and_19_out, not_11_out, not_12_out, Bit3, not_13_out);
  or or_3 (c, and_19_out, and_20_out);
  and and_20 (and_20_out, Bit1, Bit2, Bit3, not_14_out);
  or or_4 (d, and_1_out, and_2_out, and_3_out);
  or or_5 (e, Bit4, and_4_out);
  or or_6 (f, and_5_out, and_6_out, and_7_out, and_8_out, and_9_out);
  or or_7 (g, and_10_out, and_11_out, and_12_out);
endmodule

module Codificador (
  input  Bit0,
  input  Bit1,
  input  Bit2,
  input  Bit3,
  input  Bit4,
  output Bit01,
  output Bit02,
  output Bit03,
  output Bit04,
  output Bit11,
  output Bit12,
  output Bit13,
  output Bit14
);

  wire and_1_out, and_2_out, and_3_out, and_4_out, and_5_out, and_6_out, and_7_out, and_8_out, and_9_out,
       and_10_out, and_11_out, and_12_out, and_13_out, and_14_out, and_15_out, and_16_out, and_17_out,
       and_18_out, and_19_out, and_20_out, and_21_out, and_22_out, not_1_out, not_2_out, not_3_out,
       not_4_out, not_5_out, not_6_out, not_7_out, not_8_out, not_9_out, not_10_out, not_11_out, not_12_out,
       not_13_out, not_14_out, not_15_out, not_16_out, not_17_out, not_18_out, not_19_out, not_20_out,
       not_21_out, not_22_out, not_23_out, not_24_out, not_25_out, not_26_out, not_27_out, not_28_out,
       not_29_out, not_30_out, not_31_out, not_32_out, not_33_out, not_34_out, not_35_out, not_36_out,
       not_37_out, not_38_out, not_39_out, not_40_out, not_41_out, not_42_out, not_43_out;

  not not_1 (not_1_out, Bit0);
  not not_2 (not_2_out, Bit0);
  not not_3 (not_3_out, Bit1);
  not not_4 (not_4_out, Bit2);
  not not_5 (not_5_out, Bit1);
  not not_6 (not_6_out, Bit3);
  not not_7 (not_7_out, Bit1);
  not not_8 (not_8_out, Bit4);
  not not_9 (not_9_out, Bit0);
  not not_10 (not_10_out, Bit2);
  not not_11 (not_11_out, Bit3);
  not not_12 (not_12_out, Bit0);
  not not_13 (not_13_out, Bit2);
  not not_14 (not_14_out, Bit4);
  not not_15 (not_15_out, Bit2);
  not not_16 (not_16_out, Bit3);
  not not_17 (not_17_out, Bit4);
  not not_18 (not_18_out, Bit1);
  not not_19 (not_19_out, Bit0);
  not not_20 (not_20_out, Bit1);
  not not_21 (not_21_out, Bit0);
  not not_22 (not_22_out, Bit1);
  not not_23 (not_23_out, Bit2);
  not not_24 (not_24_out, Bit3);
  not not_25 (not_25_out, Bit2);
  not not_26 (not_26_out, Bit4);
  not not_27 (not_27_out, Bit2);
  not not_28 (not_28_out, Bit3);
  not not_29 (not_29_out, Bit4);
  not not_30 (not_30_out, Bit0);
  not not_31 (not_31_out, Bit1);
  not not_32 (not_32_out, Bit0);
  not not_33 (not_33_out, Bit2);
  not not_34 (not_34_out, Bit4);
  not not_35 (not_35_out, Bit1);
  not not_36 (not_36_out, Bit2);
  not not_37 (not_37_out, Bit0);
  not not_38 (not_38_out, Bit3);
  not not_39 (not_39_out, Bit1);
  not not_40 (not_40_out, Bit3);
  not not_41 (not_41_out, Bit4);
  not not_42 (not_42_out, Bit3);
  not not_43 (not_43_out, Bit4);
  and and_1 (and_1_out, not_1_out, Bit1, Bit3);
  and and_2 (and_2_out, not_2_out, Bit1, Bit2);
  and and_3 (and_3_out, Bit0, not_3_out, not_4_out);
  and and_4 (and_4_out, Bit0, not_5_out, not_6_out);
  and and_5 (and_5_out, Bit0, not_7_out, not_8_out);
  and and_6 (and_6_out, not_9_out, Bit1, not_10_out, not_11_out);
  and and_7 (and_7_out, not_12_out, Bit1, not_13_out, not_14_out);
  and and_8 (and_8_out, Bit1, not_15_out, not_16_out, not_17_out);
  and and_9 (and_9_out, Bit0, not_18_out, Bit2, Bit3, Bit4);
  and and_10 (and_10_out, not_19_out, not_20_out, Bit2);
  and and_11 (and_11_out, not_21_out, Bit2, Bit3);
  and and_12 (and_12_out, Bit0, not_22_out, not_23_out, not_24_out);
  and and_13 (and_13_out, Bit0, not_25_out, Bit3, not_26_out);
  and and_14 (and_14_out, Bit0, Bit1, not_27_out, Bit4);
  and and_15 (and_15_out, Bit0, Bit1, Bit2, not_28_out, not_29_out);
  and and_16 (and_16_out, not_30_out, not_31_out, Bit3);
  and and_17 (and_17_out, not_32_out, not_33_out, Bit3, not_34_out);
  and and_18 (and_18_out, not_35_out, not_36_out, Bit3, Bit4);
  and and_19 (and_19_out, not_37_out, Bit1, Bit2, not_38_out);
  and and_20 (and_20_out, Bit0, not_39_out, not_40_out, not_41_out);
  and and_21 (and_21_out, Bit0, Bit1, not_42_out, Bit4);
  and and_22 (and_22_out, Bit0, Bit1, Bit3, not_43_out);
  or or_1 (Bit04, and_1_out, and_2_out, and_3_out, and_4_out, and_5_out);
  or or_2 (Bit11, and_6_out, and_7_out, and_8_out, and_9_out);
  or or_3 (Bit12, and_10_out, and_11_out, and_12_out, and_13_out, and_14_out, and_15_out);
  or or_4 (Bit13, and_16_out, and_17_out, and_18_out, and_19_out, and_20_out, and_21_out, and_22_out);

  assign Bit01 = 1'b0;
  assign Bit02 = 1'b0;
  assign Bit03 = 1'b0;
  assign Bit14 = Bit4;
endmodule

module DecodificadorGeral (
  input  Bit0,
  input  Bit1,
  input  Bit2,
  input  Bit3,
  output a,
  output f,
  output b,
  output g,
  output e,
  output c,
  output d
);

  wire and_1_out, and_2_out, and_3_out, and_4_out, and_5_out, and_6_out, and_7_out, and_8_out, and_9_out,
       and_10_out, and_11_out, and_12_out, and_13_out, and_14_out, and_15_out, and_16_out, and_17_out,
       and_18_out, and_19_out, and_20_out, and_21_out, and_22_out, and_23_out, and_24_out, and_25_out,
       and_26_out, not_1_out, not_2_out, not_3_out, not_4_out, not_5_out, not_6_out, not_7_out, not_8_out,
       not_9_out, not_10_out, not_11_out, not_12_out, not_13_out, not_14_out, not_15_out, not_16_out,
       not_17_out, not_18_out, not_19_out, not_20_out;

  not not_1 (not_1_out, Bit0);
  not not_2 (not_2_out, Bit1);
  not not_3 (not_3_out, Bit2);
  not not_4 (not_4_out, Bit2);
  not not_5 (not_5_out, Bit3);
  not not_6 (not_6_out, Bit2);
  and and_1 (and_1_out, Bit1, not_6_out, Bit3);
  and and_2 (and_2_out, Bit1, Bit2, not_7_out);
  not not_7 (not_7_out, Bit3);
  and and_3 (and_3_out, Bit0, Bit2);
  and and_4 (and_4_out, Bit0, Bit1);
  not not_8 (not_8_out, Bit1);
  and and_5 (and_5_out, not_8_out, Bit2, not_9_out);
  not not_9 (not_9_out, Bit3);
  and and_6 (and_6_out, Bit0, Bit2);
  and and_7 (and_7_out, Bit0, Bit1);
  not not_10 (not_10_out, Bit1);
  and and_8 (and_8_out, not_10_out, not_11_out, Bit3);
  not not_11 (not_11_out, Bit2);
  not not_12 (not_12_out, Bit2);
  and and_9 (and_9_out, Bit1, not_12_out, not_13_out);
  not not_13 (not_13_out, Bit3);
  and and_10 (and_10_out, Bit1, Bit2, Bit3);
  and and_11 (and_11_out, Bit0, Bit2);
  and and_12 (and_12_out, Bit0, Bit1);
  and and_13 (and_13_out, Bit1, not_14_out);
  not not_14 (not_14_out, Bit2);
  and and_14 (and_14_out, Bit0, Bit2);
  not not_15 (not_15_out, Bit0);
  and and_15 (and_15_out, not_15_out, not_16_out, Bit3);
  not not_16 (not_16_out, Bit1);
  not not_17 (not_17_out, Bit1);
  and and_16 (and_16_out, not_17_out, Bit2);
  and and_17 (and_17_out, Bit2, Bit3);
  and and_18 (and_18_out, Bit0, Bit1);
  not not_18 (not_18_out, Bit0);
  and and_19 (and_19_out, not_18_out, not_19_out, not_20_out);
  not not_19 (not_19_out, Bit1);
  not not_20 (not_20_out, Bit2);
  and and_20 (and_20_out, Bit1, Bit2, Bit3);
  and and_21 (and_21_out, Bit0, Bit2);
  and and_22 (and_22_out, Bit0, Bit1);
  and and_23 (and_23_out, not_1_out, not_2_out, not_3_out, Bit3);
  and and_24 (and_24_out, Bit1, not_4_out, not_5_out);
  and and_25 (and_25_out, Bit0, Bit2);
  and and_26 (and_26_out, Bit0, Bit1);
  or or_1 (b, and_1_out, and_2_out, and_3_out, and_4_out);
  or or_2 (c, and_5_out, and_6_out, and_7_out);
  or or_3 (d, and_8_out, and_9_out, and_10_out, and_11_out, and_12_out);
  or or_4 (e, Bit3, and_13_out, and_14_out);
  or or_5 (f, and_15_out, and_16_out, and_17_out, and_18_out);
  or or_6 (g, and_19_out, and_20_out, and_21_out, and_22_out);
  or or_7 (a, and_23_out, and_24_out, and_25_out, and_26_out);
endmodule
